// Logisim project 16 BIT SUBTRACTOR.circ as structural Verilog: 1 circuit, main circuit 16 bit subtractor
module _16_bit_subtractor (
  input  A4,
  input  B4,
  input  A5,
  input  B5,
  input  A6,
  input  B6,
  input  A7,
  input  B7,
  input  A8,
  input  B8,
  input  A9,
  input  B9,
  input  A10,
  input  B10,
  input  A11,
  input  B11,
  input  A12,
  input  B12,
  input  A13,
  input  B13,
  input  A14,
  input  B14,
  input  A15,
  input  B15,
  input  A0,
  input  B0,
  input  A1,
  input  B1,
  input  A2,
  input  B2,
  input  A3,
  input  B3,
  input  M
);

  wire and_1_out, and_2_out, and_3_out, and_4_out, and_5_out, and_6_out, and_7_out, and_8_out, and_9_out,
       and_10_out, and_11_out, and_12_out, and_13_out, and_14_out, and_15_out, and_16_out, and_17_out,
       and_18_out, and_19_out, and_20_out, and_21_out, and_22_out, and_23_out, and_24_out, and_25_out,
       and_26_out, and_27_out, and_28_out, and_29_out, and_30_out, and_31_out, and_32_out, or_1_out,
       or_2_out, or_3_out, or_4_out, or_5_out, or_6_out, or_7_out, or_8_out, or_9_out, or_10_out, or_11_out,
       or_12_out, or_13_out, or_14_out, or_15_out, or_16_out, xor_1_out, xor_2_out, xor_3_out, xor_4_out,
       xor_5_out, xor_6_out, xor_7_out, xor_8_out, xor_9_out, xor_10_out, xor_11_out, xor_12_out, xor_13_out,
       xor_14_out, xor_15_out, xor_16_out, xor_17_out, xor_18_out, xor_19_out, xor_20_out, xor_21_out,
       xor_22_out, xor_23_out, xor_24_out, xor_25_out, xor_26_out, xor_27_out, xor_28_out, xor_29_out,
       xor_30_out, xor_31_out, xor_32_out, xor_33_out, xor_34_out, xor_35_out, xor_36_out, xor_37_out,
       xor_38_out, xor_39_out, xor_40_out, xor_41_out, xor_42_out, xor_43_out, xor_44_out, xor_45_out,
       xor_46_out, xor_47_out, xor_48_out;

  and and_1 (and_1_out, A0, xor_1_out);
  and and_2 (and_2_out, xor_2_out, M);
  or or_1 (or_1_out, and_1_out, and_2_out);
  xor xor_1 (xor_1_out, M, B0);
  xor xor_2 (xor_2_out, A0, xor_1_out);
  xor xor_3 (xor_3_out, M, xor_2_out);
  LED S0 (.in(xor_3_out));
  and and_3 (and_3_out, A1, xor_4_out);
  or or_2 (or_2_out, and_3_out, and_4_out);
  xor xor_4 (xor_4_out, M, B1);
  and and_4 (and_4_out, xor_5_out, or_1_out);
  xor xor_5 (xor_5_out, A1, xor_4_out);
  xor xor_6 (xor_6_out, or_1_out, xor_5_out);
  LED S1 (.in(xor_6_out));
  xor xor_7 (xor_7_out, M, B2);
  and and_5 (and_5_out, A2, xor_7_out);
  or or_3 (or_3_out, and_5_out, and_6_out);
  and and_6 (and_6_out, xor_8_out, or_2_out);
  xor xor_8 (xor_8_out, A2, xor_7_out);
  xor xor_9 (xor_9_out, or_2_out, xor_8_out);
  LED S2 (.in(xor_9_out));
  and and_7 (and_7_out, A3, xor_10_out);
  xor xor_10 (xor_10_out, M, B3);
  and and_8 (and_8_out, xor_11_out, or_3_out);
  or or_4 (or_4_out, and_7_out, and_8_out);
  xor xor_11 (xor_11_out, A3, xor_10_out);
  xor xor_12 (xor_12_out, or_3_out, xor_11_out);
  LED S3 (.in(xor_12_out));
  and and_9 (and_9_out, A4, xor_13_out);
  or or_5 (or_5_out, and_9_out, and_10_out);
  xor xor_13 (xor_13_out, M, B4);
  and and_10 (and_10_out, xor_14_out, or_4_out);
  xor xor_14 (xor_14_out, A4, xor_13_out);
  xor xor_15 (xor_15_out, or_4_out, xor_14_out);
  LED S4 (.in(xor_15_out));
  and and_11 (and_11_out, A5, xor_16_out);
  or or_6 (or_6_out, and_11_out, and_12_out);
  xor xor_16 (xor_16_out, M, B5);
  and and_12 (and_12_out, xor_17_out, or_5_out);
  xor xor_17 (xor_17_out, A5, xor_16_out);
  xor xor_18 (xor_18_out, or_5_out, xor_17_out);
  LED S5 (.in(xor_18_out));
  and and_13 (and_13_out, A6, xor_19_out);
  xor xor_19 (xor_19_out, M, B6);
  and and_14 (and_14_out, xor_20_out, or_6_out);
  or or_7 (or_7_out, and_13_out, and_14_out);
  xor xor_20 (xor_20_out, A6, xor_19_out);
  xor xor_21 (xor_21_out, or_6_out, xor_20_out);
  LED S6 (.in(xor_21_out));
  and and_15 (and_15_out, A7, xor_22_out);
  and and_16 (and_16_out, xor_24_out, or_7_out);
  or or_8 (or_8_out, and_15_out, and_16_out);
  xor xor_22 (xor_22_out, B7, M);
  xor xor_23 (xor_23_out, or_7_out, xor_24_out);
  LED S7 (.in(xor_23_out));
  xor xor_24 (xor_24_out, A7, xor_22_out);
  and and_17 (and_17_out, A8, xor_25_out);
  or or_9 (or_9_out, and_17_out, and_18_out);
  and and_18 (and_18_out, xor_26_out, or_8_out);
  xor xor_25 (xor_25_out, M, B8);
  xor xor_26 (xor_26_out, A8, xor_25_out);
  xor xor_27 (xor_27_out, or_8_out, xor_26_out);
  LED S8 (.in(xor_27_out));
  and and_19 (and_19_out, A9, xor_28_out);
  and and_20 (and_20_out, xor_30_out, or_9_out);
  or or_10 (or_10_out, and_19_out, and_20_out);
  xor xor_28 (xor_28_out, M, B9);
  xor xor_29 (xor_29_out, or_9_out, xor_30_out);
  LED S9 (.in(xor_29_out));
  xor xor_30 (xor_30_out, A9, xor_28_out);
  and and_21 (and_21_out, A10, xor_31_out);
  and and_22 (and_22_out, xor_32_out, or_10_out);
  or or_11 (or_11_out, and_21_out, and_22_out);
  xor xor_31 (xor_31_out, M, B10);
  xor xor_32 (xor_32_out, A10, xor_31_out);
  xor xor_33 (xor_33_out, or_10_out, xor_32_out);
  LED S10 (.in(xor_33_out));
  and and_23 (and_23_out, A11, xor_34_out);
  or or_12 (or_12_out, and_23_out, and_24_out);
  and and_24 (and_24_out, xor_35_out, or_11_out);
  xor xor_34 (xor_34_out, M, B11);
  xor xor_35 (xor_35_out, A11, xor_34_out);
  xor xor_36 (xor_36_out, or_11_out, xor_35_out);
  LED S11 (.in(xor_36_out));
  and and_25 (and_25_out, xor_39_out, or_12_out);
  and and_26 (and_26_out, A12, xor_38_out);
  or or_13 (or_13_out, and_26_out, and_25_out);
  xor xor_37 (xor_37_out, or_12_out, xor_39_out);
  LED S12 (.in(xor_37_out));
  xor xor_38 (xor_38_out, M, B12);
  xor xor_39 (xor_39_out, A12, xor_38_out);
  and and_27 (and_27_out, A13, xor_40_out);
  or or_14 (or_14_out, and_27_out, and_28_out);
  and and_28 (and_28_out, xor_41_out, or_13_out);
  xor xor_40 (xor_40_out, M, B13);
  xor xor_41 (xor_41_out, A13, xor_40_out);
  xor xor_42 (xor_42_out, or_13_out, xor_41_out);
  LED S13 (.in(xor_42_out));
  and and_29 (and_29_out, A14, xor_43_out);
  and and_30 (and_30_out, xor_44_out, or_14_out);
  or or_15 (or_15_out, and_29_out, and_30_out);
  xor xor_43 (xor_43_out, M, B14);
  xor xor_44 (xor_44_out, A14, xor_43_out);
  xor xor_45 (xor_45_out, or_14_out, xor_44_out);
  LED S14 (.in(xor_45_out));
  and and_31 (and_31_out, A15, A15, xor_46_out);
  or or_16 (or_16_out, and_31_out, and_32_out);
  LED COUT (.in(or_16_out));
  and and_32 (and_32_out, xor_47_out, or_15_out);
  xor xor_46 (xor_46_out, M, B15);
  xor xor_47 (xor_47_out, A15, xor_46_out);
  xor xor_48 (xor_48_out, or_15_out, xor_47_out);
  LED S15 (.in(xor_48_out));
endmodule
