// Logisim project OMAR LOGISIM.circ as structural Verilog: 1 circuit, main circuit main
module main (
  input  in_1,
  input  A,
  input  in_3,
  input  in_4,
  input  in_5,
  input  in_6,
  input  in_7,
  input  in_8,
  input  in_9,
  input  in_10,
  input  in_11,
  input  in_12,
  input  in_13,
  input  in_14,
  input  in_15,
  input  in_16,
  input  in_17,
  input  in_18,
  input  in_19,
  input  in_20,
  input  in_21,
  input  in_22,
  input  in_23,
  input  in_24,
  input  in_25,
  input  in_26,
  input  in_27,
  input  in_28,
  input  in_29,
  input  in_30,
  input  in_31,
  input  in_32,
  input  in_33,
  output out_34,
  output out_35,
  output out_36,
  output out_37,
  output out_38,
  output out_39,
  output out_40,
  output out_41,
  output out_42,
  output out_43,
  output out_44,
  output out_45,
  output out_46,
  output out_47,
  output out_48,
  output out_49,
  output out_50
);

  wire ic_74283_1_p14, ic_74283_2_p14, ic_74283_3_p14, xor_1_out, xor_2_out, xor_3_out, xor_4_out, xor_5_out,
       xor_6_out, xor_7_out, xor_8_out, xor_9_out, xor_10_out, xor_11_out, xor_12_out, xor_13_out,
       xor_14_out, xor_15_out, xor_16_out;

  xor xor_1 (xor_1_out, in_19, in_1);
  xor xor_2 (xor_2_out, in_20, in_1);
  xor xor_3 (xor_3_out, in_23, in_1);
  xor xor_4 (xor_4_out, in_24, in_1);
  xor xor_5 (xor_5_out, in_18, in_1);
  xor xor_6 (xor_6_out, in_21, in_1);
  xor xor_7 (xor_7_out, in_22, in_1);
  xor xor_8 (xor_8_out, in_25, in_1);
  xor xor_9 (xor_9_out, in_26, in_1);
  xor xor_10 (xor_10_out, in_27, in_1);
  xor xor_11 (xor_11_out, in_28, in_1);
  xor xor_12 (xor_12_out, in_29, in_1);
  xor xor_13 (xor_13_out, in_30, in_1);
  xor xor_14 (xor_14_out, in_31, in_1);
  xor xor_15 (xor_15_out, in_32, in_1);
  xor xor_16 (xor_16_out, in_33, in_1);
  // IC_74283 ic_74283_1: pin names not known; wires that end beside it: A, in_3, in_4, in_5, xor_5_out, xor_1_out, xor_2_out, xor_6_out, in_1, out_50, out_49, out_48, out_47, ic_74283_1_p14
  // IC_74283 ic_74283_2: pin names not known; wires that end beside it: in_6, in_7, in_8, in_9, xor_7_out, xor_3_out, xor_4_out, xor_8_out, ic_74283_1_p14, out_46, out_45, out_44, out_43, ic_74283_2_p14
  // IC_74283 ic_74283_3: pin names not known; wires that end beside it: in_10, in_11, in_12, in_13, xor_9_out, xor_10_out, xor_11_out, xor_12_out, ic_74283_2_p14, out_42, out_41, out_40, out_39, ic_74283_3_p14
  // IC_74283 ic_74283_4: pin names not known; wires that end beside it: in_14, in_15, in_16, in_17, xor_13_out, xor_14_out, xor_15_out, xor_16_out, ic_74283_3_p14, out_38, out_37, out_36, out_35, out_34

  // Notes on the sheet:
  //   B
endmodule
